// Logisim project control_word_decoder.circ as structural Verilog: 1 circuit, main circuit control_word_decoder
module control_word_decoder (
  input  [31:0] cw_dp__0,
  input  [31:0] cw_dp__1,
  output [3:0] ir_load_n,
  output [15:0] left_src_n,
  output [3:0] left_lane_n,
  output [7:0] right_src_n,
  output [15:0] alu_op_n,
  output [7:0] alu_shift_n,
  output [3:0] v_src_n,
  output [3:0] c_src_n,
  output [3:0] cc_write_n,
  output [3:0] cc_mi_n,
  output [15:0] z_dest_n,
  output [3:0] z_lane_n,
  output [3:0] pc_ctrl_n,
  output [3:0] mar_ctrl_n,
  output [3:0] x_ctrl_n,
  output [3:0] y_ctrl_n,
  output [3:0] mem_op_n,
  output [3:0] mmu_addr_n,
  output [3:0] mmu_map_n,
  output [3:0] mmu_pt_n,
  output alu_cin,
  output alu_width,
  output [4:0] flag_we,
  output z_accum,
  output sp_bank,
  output tas_lock
);

  wire ONE, ZERO;

  _74138 a_sh (
    .pin1(cw_dp__0[15]), .pin2(cw_dp__0[16]), .pin3(cw_dp__0[17]), .pin4(ZERO), .pin5(ZERO), .pin6(ONE),
    .pin7(alu_shift_n[7]), .pin15(alu_shift_n[0]), .pin14(alu_shift_n[1]), .pin13(alu_shift_n[2]),
    .pin12(alu_shift_n[3]), .pin11(alu_shift_n[4]), .pin10(alu_shift_n[5]), .pin9(alu_shift_n[6]));
  _74139 d3 (
    .pin1(ZERO), .pin2(cw_dp__1[6]), .pin3(cw_dp__1[7]), .pin4(z_lane_n[0]), .pin5(z_lane_n[1]),
    .pin6(z_lane_n[2]), .pin7(z_lane_n[3]), .pin15(ZERO), .pin14(cw_dp__1[8]), .pin13(cw_dp__1[9]),
    .pin12(pc_ctrl_n[0]), .pin11(pc_ctrl_n[1]), .pin10(pc_ctrl_n[2]), .pin9(pc_ctrl_n[3]));
  _74139 d7 (
    .pin1(ZERO), .pin2(cw_dp__1[22]), .pin3(cw_dp__1[23]), .pin4(mmu_pt_n[0]), .pin5(mmu_pt_n[1]),
    .pin6(mmu_pt_n[2]), .pin7(mmu_pt_n[3]), .pin15(ONE), .pin14(ZERO), .pin13(ZERO));  // open: pin12, pin11, pin10, pin9
  _74138 op_lo (
    .pin1(cw_dp__0[11]), .pin2(cw_dp__0[12]), .pin3(cw_dp__0[13]), .pin4(cw_dp__0[14]), .pin5(ZERO),
    .pin6(ONE), .pin7(alu_op_n[7]), .pin15(alu_op_n[0]), .pin14(alu_op_n[1]), .pin13(alu_op_n[2]),
    .pin12(alu_op_n[3]), .pin11(alu_op_n[4]), .pin10(alu_op_n[5]), .pin9(alu_op_n[6]));
  _74139 d0 (
    .pin1(ZERO), .pin2(cw_dp__0[0]), .pin3(cw_dp__0[1]), .pin4(ir_load_n[0]), .pin5(ir_load_n[1]),
    .pin6(ir_load_n[2]), .pin7(ir_load_n[3]), .pin15(ZERO), .pin14(cw_dp__0[6]), .pin13(cw_dp__0[7]),
    .pin12(left_lane_n[0]), .pin11(left_lane_n[1]), .pin10(left_lane_n[2]), .pin9(left_lane_n[3]));
  _74139 d4 (
    .pin1(ZERO), .pin2(cw_dp__1[10]), .pin3(cw_dp__1[11]), .pin4(mar_ctrl_n[0]), .pin5(mar_ctrl_n[1]),
    .pin6(mar_ctrl_n[2]), .pin7(mar_ctrl_n[3]), .pin15(ZERO), .pin14(cw_dp__1[12]), .pin13(cw_dp__1[13]),
    .pin12(x_ctrl_n[0]), .pin11(x_ctrl_n[1]), .pin10(x_ctrl_n[2]), .pin9(x_ctrl_n[3]));
  _74138 ls_hi (
    .pin1(cw_dp__0[2]), .pin2(cw_dp__0[3]), .pin3(cw_dp__0[4]), .pin4(ZERO), .pin5(ZERO), .pin6(cw_dp__0[5]),
    .pin7(left_src_n[15]), .pin15(left_src_n[8]), .pin14(left_src_n[9]), .pin13(left_src_n[10]),
    .pin12(left_src_n[11]), .pin11(left_src_n[12]), .pin10(left_src_n[13]), .pin9(left_src_n[14]));
  _74138 r_src (
    .pin1(cw_dp__0[8]), .pin2(cw_dp__0[9]), .pin3(cw_dp__0[10]), .pin4(ZERO), .pin5(ZERO), .pin6(ONE),
    .pin7(right_src_n[7]), .pin15(right_src_n[0]), .pin14(right_src_n[1]), .pin13(right_src_n[2]),
    .pin12(right_src_n[3]), .pin11(right_src_n[4]), .pin10(right_src_n[5]), .pin9(right_src_n[6]));
  _74139 d1 (
    .pin1(ZERO), .pin2(cw_dp__0[25]), .pin3(cw_dp__0[26]), .pin4(v_src_n[0]), .pin5(v_src_n[1]),
    .pin6(v_src_n[2]), .pin7(v_src_n[3]), .pin15(ZERO), .pin14(cw_dp__0[27]), .pin13(cw_dp__0[28]),
    .pin12(c_src_n[0]), .pin11(c_src_n[1]), .pin10(c_src_n[2]), .pin9(c_src_n[3]));
  _74139 d5 (
    .pin1(ZERO), .pin2(cw_dp__1[14]), .pin3(cw_dp__1[15]), .pin4(y_ctrl_n[0]), .pin5(y_ctrl_n[1]),
    .pin6(y_ctrl_n[2]), .pin7(y_ctrl_n[3]), .pin15(ZERO), .pin14(cw_dp__1[16]), .pin13(cw_dp__1[17]),
    .pin12(mem_op_n[0]), .pin11(mem_op_n[1]), .pin10(mem_op_n[2]), .pin9(mem_op_n[3]));
  _74138 ls_lo (
    .pin1(cw_dp__0[2]), .pin2(cw_dp__0[3]), .pin3(cw_dp__0[4]), .pin4(cw_dp__0[5]), .pin5(ZERO), .pin6(ONE),
    .pin7(left_src_n[7]), .pin15(left_src_n[0]), .pin14(left_src_n[1]), .pin13(left_src_n[2]),
    .pin12(left_src_n[3]), .pin11(left_src_n[4]), .pin10(left_src_n[5]), .pin9(left_src_n[6]));
  _74138 zd_hi (
    .pin1(cw_dp__1[2]), .pin2(cw_dp__1[3]), .pin3(cw_dp__1[4]), .pin4(ZERO), .pin5(ZERO), .pin6(cw_dp__1[5]),
    .pin7(z_dest_n[15]), .pin15(z_dest_n[8]), .pin14(z_dest_n[9]), .pin13(z_dest_n[10]),
    .pin12(z_dest_n[11]), .pin11(z_dest_n[12]), .pin10(z_dest_n[13]), .pin9(z_dest_n[14]));
  _74139 d2 (
    .pin1(ZERO), .pin2(cw_dp__0[30]), .pin3(cw_dp__0[31]), .pin4(cc_write_n[0]), .pin5(cc_write_n[1]),
    .pin6(cc_write_n[2]), .pin7(cc_write_n[3]), .pin15(ZERO), .pin14(cw_dp__1[0]), .pin13(cw_dp__1[1]),
    .pin12(cc_mi_n[0]), .pin11(cc_mi_n[1]), .pin10(cc_mi_n[2]), .pin9(cc_mi_n[3]));
  _74139 d6 (
    .pin1(ZERO), .pin2(cw_dp__1[18]), .pin3(cw_dp__1[19]), .pin4(mmu_addr_n[0]), .pin5(mmu_addr_n[1]),
    .pin6(mmu_addr_n[2]), .pin7(mmu_addr_n[3]), .pin15(ZERO), .pin14(cw_dp__1[20]), .pin13(cw_dp__1[21]),
    .pin12(mmu_map_n[0]), .pin11(mmu_map_n[1]), .pin10(mmu_map_n[2]), .pin9(mmu_map_n[3]));
  _74138 op_hi (
    .pin1(cw_dp__0[11]), .pin2(cw_dp__0[12]), .pin3(cw_dp__0[13]), .pin4(ZERO), .pin5(ZERO),
    .pin6(cw_dp__0[14]), .pin7(alu_op_n[15]), .pin15(alu_op_n[8]), .pin14(alu_op_n[9]), .pin13(alu_op_n[10]),
    .pin12(alu_op_n[11]), .pin11(alu_op_n[12]), .pin10(alu_op_n[13]), .pin9(alu_op_n[14]));
  _74138 zd_lo (
    .pin1(cw_dp__1[2]), .pin2(cw_dp__1[3]), .pin3(cw_dp__1[4]), .pin4(cw_dp__1[5]), .pin5(ZERO), .pin6(ONE),
    .pin7(z_dest_n[7]), .pin15(z_dest_n[0]), .pin14(z_dest_n[1]), .pin13(z_dest_n[2]), .pin12(z_dest_n[3]),
    .pin11(z_dest_n[4]), .pin10(z_dest_n[5]), .pin9(z_dest_n[6]));

  assign alu_cin = cw_dp__0[18];
  assign alu_width = cw_dp__0[19];
  assign flag_we = cw_dp__0[24:20];
  assign sp_bank = cw_dp__1[24];
  assign tas_lock = cw_dp__1[25];
  assign z_accum = cw_dp__0[29];
  // also tied to GND on the sheet: ZERO
  // also tied to VCC on the sheet: ONE
endmodule
