// Logisim project microsequencer.circ as structural Verilog: 1 circuit, main circuit microsequencer
module microsequencer (
  input  clk,
  input  clr_n,
  input  [2:0] useq_op,
  input  [11:0] next_addr,
  input  [3:0] ucond_sel,
  input  ucond_pol,
  input  [15:0] cond,
  input  [11:0] lut_data,
  output [11:0] upc
);

  wire cond_hi, cond_lo, ONE, ZERO;
  wire [2:0] upc_rco;
  wire [3:0] and_y, merge_y, or_y, xor_y;
  wire [4:4] inv_a;
  wire [5:0] inv_y;
  wire [7:0] op_n;
  wire [11:0] p;

  _7408 brand (
    .pin1(inv_y[0]), .pin2(xor_y[0]), .pin3(and_y[0]), .pin4(ZERO), .pin5(ZERO), .pin6(and_y[1]),
    .pin13(ZERO), .pin12(ZERO), .pin11(and_y[3]), .pin10(ZERO), .pin9(ZERO), .pin8(and_y[2]));
  _7486 cpol (
    .pin1(merge_y[0]), .pin2(ucond_pol), .pin3(xor_y[0]), .pin4(ZERO), .pin5(ZERO), .pin6(xor_y[1]),
    .pin13(ZERO), .pin12(ZERO), .pin11(xor_y[3]), .pin10(ZERO), .pin9(ZERO), .pin8(xor_y[2]));
  _74153 nmux_1__m (
    .pin1(ZERO), .pin2(inv_y[3]), .pin3(ZERO), .pin4(ZERO), .pin5(lut_data[2]), .pin6(next_addr[2]),
    .pin7(p[2]), .pin15(inv_y[2]), .pin14(ZERO), .pin13(ZERO), .pin12(ZERO), .pin11(lut_data[3]),
    .pin10(next_addr[3]), .pin9(p[3]));
  _74153 nmux_5__m (
    .pin1(ZERO), .pin2(inv_y[3]), .pin3(ZERO), .pin4(ZERO), .pin5(lut_data[10]), .pin6(next_addr[10]),
    .pin7(p[10]), .pin15(inv_y[2]), .pin14(ZERO), .pin13(ZERO), .pin12(ZERO), .pin11(lut_data[11]),
    .pin10(next_addr[11]), .pin9(p[11]));
  _74138 useq (
    .pin1(useq_op[0]), .pin2(useq_op[1]), .pin3(useq_op[2]), .pin4(ZERO), .pin5(ZERO), .pin6(ONE),
    .pin7(op_n[7]), .pin15(op_n[0]), .pin14(op_n[1]), .pin13(op_n[2]), .pin12(op_n[3]), .pin11(op_n[4]),
    .pin10(op_n[5]), .pin9(op_n[6]));
  _74157 cmerge (
    .pin1(ucond_sel[3]), .pin2(cond_lo), .pin3(cond_hi), .pin4(merge_y[0]), .pin5(ZERO), .pin6(ZERO),
    .pin7(merge_y[1]), .pin15(ZERO), .pin14(ZERO), .pin13(ZERO), .pin12(merge_y[3]), .pin11(ZERO),
    .pin10(ZERO), .pin9(merge_y[2]));
  _7404 inv (
    .pin1(op_n[1]), .pin2(inv_y[0]), .pin3(op_n[2]), .pin4(inv_y[1]), .pin5(op_n[3]), .pin6(inv_y[2]),
    .pin13(ZERO), .pin12(inv_y[5]), .pin11(inv_a[4]), .pin10(inv_y[4]), .pin9(op_n[4]), .pin8(inv_y[3]));
  _74153 nmux_2__m (
    .pin1(ZERO), .pin2(inv_y[3]), .pin3(ZERO), .pin4(ZERO), .pin5(lut_data[4]), .pin6(next_addr[4]),
    .pin7(p[4]), .pin15(inv_y[2]), .pin14(ZERO), .pin13(ZERO), .pin12(ZERO), .pin11(lut_data[5]),
    .pin10(next_addr[5]), .pin9(p[5]));
  _74161 u0 (
    .pin1(clr_n), .pin2(clk), .pin3(p[0]), .pin4(p[1]), .pin5(p[2]), .pin6(p[3]), .pin7(op_n[5]),
    .pin15(upc_rco[0]), .pin14(upc[0]), .pin13(upc[1]), .pin12(upc[2]), .pin11(upc[3]), .pin10(op_n[5]),
    .pin9(inv_y[4]));
  _74151 cmux_hi (
    .pin1(cond[11]), .pin2(cond[10]), .pin3(cond[9]), .pin4(cond[8]), .pin5(cond_hi), .pin7(ZERO),
    .pin15(cond[12]), .pin14(cond[13]), .pin13(cond[14]), .pin12(cond[15]), .pin11(ucond_sel[0]),
    .pin10(ucond_sel[1]), .pin9(ucond_sel[2]));  // open: pin6
  _7432 lor (
    .pin1(inv_y[1]), .pin2(and_y[0]), .pin3(or_y[0]), .pin4(inv_y[2]), .pin5(inv_y[3]), .pin6(or_y[1]),
    .pin13(ZERO), .pin12(ZERO), .pin11(or_y[3]), .pin10(or_y[1]), .pin9(or_y[0]), .pin8(inv_a[4]));
  _74153 nmux_3__m (
    .pin1(ZERO), .pin2(inv_y[3]), .pin3(ZERO), .pin4(ZERO), .pin5(lut_data[6]), .pin6(next_addr[6]),
    .pin7(p[6]), .pin15(inv_y[2]), .pin14(ZERO), .pin13(ZERO), .pin12(ZERO), .pin11(lut_data[7]),
    .pin10(next_addr[7]), .pin9(p[7]));
  _74161 u1 (
    .pin1(clr_n), .pin2(clk), .pin3(p[4]), .pin4(p[5]), .pin5(p[6]), .pin6(p[7]), .pin7(op_n[5]),
    .pin15(upc_rco[1]), .pin14(upc[4]), .pin13(upc[5]), .pin12(upc[6]), .pin11(upc[7]), .pin10(upc_rco[0]),
    .pin9(inv_y[4]));
  _74151 cmux_lo (
    .pin1(cond[3]), .pin2(cond[2]), .pin3(cond[1]), .pin4(cond[0]), .pin5(cond_lo), .pin7(ZERO),
    .pin15(cond[4]), .pin14(cond[5]), .pin13(cond[6]), .pin12(ONE), .pin11(ucond_sel[0]),
    .pin10(ucond_sel[1]), .pin9(ucond_sel[2]));  // open: pin6
  _74153 nmux_0__m (
    .pin1(ZERO), .pin2(inv_y[3]), .pin3(ZERO), .pin4(ZERO), .pin5(lut_data[0]), .pin6(next_addr[0]),
    .pin7(p[0]), .pin15(inv_y[2]), .pin14(ZERO), .pin13(ZERO), .pin12(ZERO), .pin11(lut_data[1]),
    .pin10(next_addr[1]), .pin9(p[1]));
  _74153 nmux_4__m (
    .pin1(ZERO), .pin2(inv_y[3]), .pin3(ZERO), .pin4(ZERO), .pin5(lut_data[8]), .pin6(next_addr[8]),
    .pin7(p[8]), .pin15(inv_y[2]), .pin14(ZERO), .pin13(ZERO), .pin12(ZERO), .pin11(lut_data[9]),
    .pin10(next_addr[9]), .pin9(p[9]));
  _74161 u2 (
    .pin1(clr_n), .pin2(clk), .pin3(p[8]), .pin4(p[9]), .pin5(p[10]), .pin6(p[11]), .pin7(op_n[5]),
    .pin15(upc_rco[2]), .pin14(upc[8]), .pin13(upc[9]), .pin12(upc[10]), .pin11(upc[11]), .pin10(upc_rco[1]),
    .pin9(inv_y[4]));
  // also tied to GND on the sheet: ZERO
  // also tied to VCC on the sheet: ONE
endmodule
